// Logisim project BealMorinValembois.circ as structural Verilog: 11 circuits, main circuit main
module main (
  input  Reset,
  input  ResetRAM
);

  wire Clock, Clock_out, Cond, CTRL, decodeir_1_call, End, Exec, Fetch, getcst_1_imm, Load,
       ramctrl_1_memload, ramctrl_1_memstore, Ret, Store, WriteReg;
  wire [2:0] GetOp;
  wire [15:0] Addr, alu_1_output, Arg01, bit_extender_2_out, getcst_1_cst, JMP_Address, MemIN,
       multiplexer_1_out, multiplexer_2_out, PC, pcheap_1_out, R0, R1, R2, R3, R4, R5, R6, R7,
       registres_1_out_sr2, regpc_1_nextpc;
  wire [31:0] bit_extender_1_out, IR, MemOUT;

  Clock u_Clock (.out(Clock_out));
  Seq seq_1 (.ClockOrig(Clock_out), .reset(Reset), .Fetch(Fetch), .Exec(Exec), .Clock(Clock));
  LED led_1 (.in(Clock_out));
  RegPC regpc_1 (
    .JMP_Address(multiplexer_1_out), .Cond(Cond), .CTRL(CTRL), .Clock(Exec), .Reset(Reset), .PC(PC),
    .NextPC(regpc_1_nextpc), .End(End));
  GetAddr getaddr_1 (.PC(PC), .Addr(Addr), .Fetch(Fetch), .Load(Load), .Store(Store), .Arg(Arg01));
  // Probe on Addr
  LED led_2 (.in(Fetch));
  LED led_3 (.in(Exec));
  Multiplexer #(.width(16), .enable("false")) multiplexer_1 (
    .in0(JMP_Address), .in1(pcheap_1_out), .out(multiplexer_1_out), .sel(Ret));
  // Probe on MemIN
  assign bit_extender_1_out = {{16{MemIN[15]}}, MemIN};  // Bit_Extender bit_extender_1
  // Probe on PC
  // Probe on IR
  PCHeap pcheap_1 (
    .Ret(Ret), .Call(decodeir_1_call), .Out(pcheap_1_out), .Reset(Reset), .In(regpc_1_nextpc), .Clock(Clock),
    .Exec(Exec));
  DecodeIR decodeir_1 (
    .CTRL(CTRL), .WriteReg(WriteReg), .IR(IR), .Load(Load), .GetOp(GetOp), .JMPAddress(JMP_Address),
    .Store(Store), .Call(decodeir_1_call), .Ret(Ret), .End(End));
  RamCtrl ramctrl_1 (
    .Store(Store), .Fetch(Fetch), .Exec(Exec), .Load(Load), .MemStore(ramctrl_1_memstore),
    .MemLoad(ramctrl_1_memload), .Clock(Clock));
  // Probe on MemOUT
  RAM #(.addrWidth(16), .dataWidth(32), .bus("separate")) ram_1 (
    .addr(Addr), .din(bit_extender_1_out), .data(MemOUT), .str(ramctrl_1_memstore), .clk(ramctrl_1_memstore),
    .ld(ramctrl_1_memload), .clr(ResetRAM));  // open: sel
  // Probe on R0
  // Probe on R3
  // Probe on R6
  Register #(.width(32), .trigger("falling")) RegIR (.D(MemOUT), .Q(IR), .clk(Fetch), .clr(Reset));  // open: en
  // Probe on R1
  // Probe on R4
  // Probe on R7
  // Probe on IR
  // Probe on R2
  // Probe on R5
  Bit_Extender #(.in_width(32), .\type ("sign")) bit_extender_2 (.in(MemOUT), .out(bit_extender_2_out));
  // Probe on IR[8:6]
  // Probe on IR[11:9]
  // Probe on IR[14:12]
  // Probe on getcst_1_cst
  GetCst getcst_1 (.IR(IR), .Cst(getcst_1_cst), .Imm(getcst_1_imm));
  Multiplexer #(.width(16), .enable("false")) multiplexer_2 (
    .in0(alu_1_output), .in1(bit_extender_2_out), .out(multiplexer_2_out), .sel(Load));
  Registres registres_1 (
    .IN(multiplexer_2_out), .WriteReg(WriteReg), .DR(IR[8:6]), .OUT_SR1(Arg01),
    .OUT_SR2(registres_1_out_sr2), .OUT_DR(MemIN), .R0(R0), .R1(R1), .R2(R2), .R3(R3), .R4(R4), .R5(R5),
    .R6(R6), .R7(R7), .Reset(Reset), .Clock(Exec), .SR1(IR[11:9]), .SR2(IR[14:12]));
  // Probe on registres_1_out_sr2
  // Probe on Arg01
  ALU alu_1 (
    .Imm(getcst_1_imm), .Op(GetOp), .Input1(Arg01), .Input2(registres_1_out_sr2), .Cst(getcst_1_cst),
    .Output(alu_1_output));
  JmpCond jmpcond_1 (.Arg0(Arg01), .Arg1(registres_1_out_sr2), .Cond(Cond), .Op(GetOp));
  // Probe on multiplexer_2_out
  // Probe on R0
  // Probe on R1
  // Probe on R2
  // Probe on R3
  // Probe on R4
  // Probe on R5
  // Probe on R6
  // Probe on R7
  // Probe on alu_1_output

  // Notes on the sheet:
  //   RAM
endmodule

module ALU (
  input  [15:0] Input1,
  input  [15:0] Input2,
  input  [15:0] Cst,
  input  Imm,
  input  [2:0] Op,
  output [15:0] Output
);

  wire [3:0] bit_extender_1_out;
  wire [15:0] adder_1_out, AND_out, multiplexer_2_out, multiplier_1_out, OR_out, shifter_1_out,
       shifter_2_out, subtractor_1_out, XOR_out;

  Bit_Extender #(.in_width(16), .out_width(4)) bit_extender_1 (.in(multiplexer_2_out), .out(bit_extender_1_out));
  Adder #(.width(16)) adder_1 (.a(Input1), .b(multiplexer_2_out), .out(adder_1_out));  // open: cin, cout
  Subtractor #(.width(16)) subtractor_1 (.a(Input1), .b(multiplexer_2_out), .out(subtractor_1_out));  // open: bin, bout
  assign AND_out = Input1 & multiplexer_2_out;  // AND_Gate AND, 16 bits wide
  assign OR_out = Input1 | multiplexer_2_out;  // OR_Gate OR, 16 bits wide
  Multiplexer #(.select(3), .width(16), .enable("false")) multiplexer_1 (
    .in0(adder_1_out), .in1(subtractor_1_out), .in2(AND_out), .in3(OR_out), .in4(XOR_out),
    .in5(shifter_1_out), .in6(shifter_2_out), .in7(multiplier_1_out), .out(Output), .sel(Op));
  Multiplexer #(.width(16), .enable("false")) multiplexer_2 (
    .in0(Input2), .in1(Cst), .out(multiplexer_2_out), .sel(Imm));
  assign XOR_out = Input1 ^ multiplexer_2_out;  // XOR_Gate XOR, 16 bits wide
  Shifter #(.width(16)) shifter_1 (.in(Input1), .\dist (bit_extender_1_out), .out(shifter_1_out));
  Shifter #(.width(16), .shift("lr")) shifter_2 (.in(Input1), .\dist (bit_extender_1_out), .out(shifter_2_out));
  // Probe on Input1
  // Probe on multiplexer_2_out
  // Probe on bit_extender_1_out
  Multiplier #(.width(16)) multiplier_1 (.a(Input1), .b(multiplexer_2_out), .out(multiplier_1_out));  // open: cin, cout
  // Probe on Output
endmodule

module DecodeIR (
  input  [31:0] IR,
  output WriteReg,
  output Store,
  output Load,
  output [2:0] GetOp,
  output Call,
  output Ret,
  output End,
  output CTRL,
  output [15:0] JMPAddress
);

  wire decoder_1_out0, decoder_1_out1, decoder_2_out0, decoder_2_out1, decoder_2_out5, decoder_2_out6,
       decoder_2_out7;
  wire [15:0] bit_extender_1_out;

  Decoder #(.select(2), .disabled(0), .enable("false")) decoder_1 (
    .out0(decoder_1_out0), .out1(decoder_1_out1), .out3(CTRL), .sel(IR[1:0]));  // open: out2
  Decoder #(.select(3), .disabled(0), .enable("false")) decoder_2 (
    .out0(decoder_2_out0), .out1(decoder_2_out1), .out5(decoder_2_out5), .out6(decoder_2_out6),
    .out7(decoder_2_out7), .sel(IR[4:2]));  // open: out2, out3, out4
  assign bit_extender_1_out = {{15{1'b1}}, CTRL};  // Bit_Extender bit_extender_1
  and and_1 (Store, decoder_1_out1, decoder_2_out0);
  and and_2 (Load, decoder_1_out1, decoder_2_out1);
  and and_3 (Call, CTRL, decoder_2_out5);
  and and_4 (Ret, decoder_2_out6, CTRL);
  and and_5 (End, decoder_2_out7, CTRL);
  assign JMPAddress = bit_extender_1_out & IR[31:16];  // AND_Gate and_6, 16 bits wide
  or or_1 (WriteReg, decoder_1_out0, Store);

  assign GetOp = IR[4:2];

  // Notes on the sheet:
  //   CTRL
  //   MEM
  //   UAL
endmodule

module GetAddr (
  input  [15:0] PC,
  input  [15:0] Arg,
  input  Load,
  input  Store,
  input  Fetch,
  output [15:0] Addr
);

  wire and_1_out, not_1_out, xor_1_out;

  xor xor_1 (xor_1_out, Load, Store);
  not not_1 (not_1_out, Fetch);
  and and_1 (and_1_out, xor_1_out, not_1_out);
  Multiplexer #(.width(16), .enable("false")) multiplexer_1 (.in0(PC), .in1(Arg), .out(Addr), .sel(and_1_out));
endmodule

module GetCst (
  input  [31:0] IR,
  output [15:0] Cst,
  output Imm
);


  assign Cst = IR[31:16];
  assign Imm = IR[5];
endmodule

module RamCtrl (
  input  Clock,
  input  Exec,
  input  Fetch,
  input  Load,
  input  Store,
  output MemLoad,
  output MemStore
);

  wire and_1_out;

  and and_1 (and_1_out, Exec, Load);
  and and_2 (MemStore, Exec, Clock, Store);
  or or_1 (MemLoad, Fetch, and_1_out);
endmodule

module Registres (
  input  [15:0] IN,
  input  [2:0] SR1,
  input  WriteReg,
  input  [2:0] SR2,
  input  [2:0] DR,
  input  Clock,
  input  Reset,
  output [15:0] R0,
  output [15:0] OUT_SR1,
  output [15:0] R1,
  output [15:0] R2,
  output [15:0] R3,
  output [15:0] OUT_SR2,
  output [15:0] R4,
  output [15:0] R5,
  output [15:0] OUT_DR,
  output [15:0] R6,
  output [15:0] R7
);

  wire demultiplexer_1_out0, demultiplexer_1_out1, demultiplexer_1_out2, demultiplexer_1_out3,
       demultiplexer_1_out4, demultiplexer_1_out5, demultiplexer_1_out6, demultiplexer_1_out7;

  Demultiplexer #(.select(3), .enable("false")) demultiplexer_1 (
    .out0(demultiplexer_1_out0), .out1(demultiplexer_1_out1), .out2(demultiplexer_1_out2),
    .out3(demultiplexer_1_out3), .out4(demultiplexer_1_out4), .out5(demultiplexer_1_out5),
    .out6(demultiplexer_1_out6), .out7(demultiplexer_1_out7), .in(WriteReg), .sel(DR));
  Register #(.width(16), .trigger("falling")) u_R0 (
    .D(IN), .en(demultiplexer_1_out0), .Q(R0), .clk(Clock), .clr(Reset));
  Register #(.width(16), .trigger("falling")) u_R1 (
    .D(IN), .en(demultiplexer_1_out1), .Q(R1), .clk(Clock), .clr(Reset));
  Register #(.width(16), .trigger("falling")) u_R2 (
    .D(IN), .en(demultiplexer_1_out2), .Q(R2), .clk(Clock), .clr(Reset));
  Register #(.width(16), .trigger("falling")) u_R3 (
    .D(IN), .en(demultiplexer_1_out3), .Q(R3), .clk(Clock), .clr(Reset));
  Register #(.width(16), .trigger("falling")) u_R4 (
    .D(IN), .en(demultiplexer_1_out4), .Q(R4), .clk(Clock), .clr(Reset));
  Register #(.width(16), .trigger("falling")) u_R5 (
    .D(IN), .en(demultiplexer_1_out5), .Q(R5), .clk(Clock), .clr(Reset));
  Register #(.width(16), .trigger("falling")) u_R6 (
    .D(IN), .en(demultiplexer_1_out6), .Q(R6), .clk(Clock), .clr(Reset));
  Register #(.width(16), .trigger("falling")) u_R7 (
    .D(IN), .en(demultiplexer_1_out7), .Q(R7), .clk(Clock), .clr(Reset));
  Multiplexer #(.select(3), .width(16), .enable("false")) multiplexer_1 (
    .in0(R0), .in1(R1), .in2(R2), .in3(R3), .in4(R4), .in5(R5), .in6(R6), .in7(R7), .out(OUT_SR1), .sel(SR1));
  Multiplexer #(.select(3), .width(16), .enable("false")) multiplexer_2 (
    .in0(R0), .in1(R1), .in2(R2), .in3(R3), .in4(R4), .in5(R5), .in6(R6), .in7(R7), .out(OUT_SR2), .sel(SR2));
  Multiplexer #(.select(3), .width(16), .enable("false")) multiplexer_3 (
    .in0(R0), .in1(R1), .in2(R2), .in3(R3), .in4(R4), .in5(R5), .in6(R6), .in7(R7), .out(OUT_DR), .sel(DR));
  // Probe on SR1
  // Probe on SR2
  // Probe on DR
endmodule

module RegPC (
  input  End,
  input  [15:0] JMP_Address,
  input  Cond,
  input  CTRL,
  input  Clock,
  input  Reset,
  output [15:0] NextPC,
  output [15:0] PC
);

  wire and_1_out, not_1_out;
  wire [15:0] multiplexer_1_out;

  not not_1 (not_1_out, End);
  Adder #(.width(16)) adder_1 (.a(PC), .b({16{1'b0}}), .out(NextPC), .cin(not_1_out));  // open: cout
  and and_1 (and_1_out, Cond, CTRL);
  Multiplexer #(.width(16), .enable("false")) multiplexer_1 (
    .in0(NextPC), .in1(JMP_Address), .out(multiplexer_1_out), .sel(and_1_out));
  Register #(.width(16), .trigger("falling")) u_PC (
    .D(multiplexer_1_out), .Q(PC), .clk(Clock), .clr(Reset));  // open: en
endmodule

module Seq (
  input  ClockOrig,
  input  reset,
  output Fetch,
  output Exec,
  output Clock
);

  Register #(.width(1), .trigger("falling")) register_1 (
    .D(Fetch), .Q(Exec), .clk(ClockOrig), .clr(reset));  // open: en
  not not_1 (Fetch, Exec);
  buf buffer_1 (Clock, ClockOrig);
endmodule

module JmpCond (
  input  [15:0] Arg0,
  input  [15:0] Arg1,
  input  [2:0] Op,
  output Cond
);

  wire comparator_1_eq, comparator_1_gt, comparator_1_lt, not_1_out;

  Comparator #(.width(16)) comparator_1 (
    .a(Arg0), .b(Arg1), .gt(comparator_1_gt), .eq(comparator_1_eq), .lt(comparator_1_lt));
  not not_1 (not_1_out, comparator_1_eq);
  Multiplexer #(.select(3), .enable("false")) multiplexer_1 (
    .in0(1'b1), .in1(comparator_1_eq), .in2(not_1_out), .in3(comparator_1_gt), .in4(comparator_1_lt),
    .in5(1'b1), .in6(1'b1), .in7(1'b0), .out(Cond), .sel(Op));

  // Notes on the sheet:
  //   Jump/Call/Ret
  //   End
endmodule

module PCHeap (
  input  [15:0] In,
  input  Ret,
  input  Reset,
  input  Call,
  input  Clock,
  input  Exec,
  output [15:0] Out
);

  wire and_1_out, and_2_out, or_1_out;
  wire [7:0] adder_1_out, HC_q, multiplexer_1_out, multiplexer_2_out;

  // Probe on In
  // Probe on 8'h1
  // Probe on {8{1'b1}}
  Multiplexer #(.width(8), .enable("false")) multiplexer_1 (
    .in0(8'h1), .in1({8{1'b1}}), .out(multiplexer_1_out), .sel(Ret));
  // Probe on multiplexer_1_out
  or or_1 (or_1_out, Ret, Call);
  Adder adder_1 (.a(HC_q), .b(multiplexer_1_out), .out(adder_1_out));  // open: cin, cout
  // Probe on adder_1_out
  and and_1 (and_1_out, or_1_out, Exec, Clock);
  // Probe on HC_q
  Register #(.trigger("falling")) HC (.D(adder_1_out), .Q(HC_q), .clk(and_1_out));  // open: en, clr
  and and_2 (and_2_out, Exec, Clock, Call);
  Multiplexer #(.width(8), .enable("false")) multiplexer_2 (
    .in0(HC_q), .in1(adder_1_out), .out(multiplexer_2_out), .sel(Ret));
  // Probe on multiplexer_2_out
  RAM #(.dataWidth(16), .bus("separate")) ram_1 (
    .addr(multiplexer_2_out), .din(In), .data(Out), .str(and_2_out), .clk(and_2_out), .ld(1'b1), .clr(Reset));  // open: sel
  // Probe on Out
endmodule
